# Fritzing sketch lamp-wire-up (saved by Fritzing 0.9.2b)
breadboards: 1

parts:
  Part1 = Arduino Uno (Rev3)
  Q1 = MOSFET-NCHANNEL [package=to220v]
  S1 = Round Pushbutton
  S2 = Round Pushbutton
  R1 = Resistor [tolerance=±5% resistance=220 package=THT]
  Q2 = MOSFET-NCHANNEL [package=to220v]

nets:
  N1: Part1.D9_PWM, S2.leg1
  N2: Part1.D10_PWM/SS, S1.leg1
  N3: Part1.D11_PWM/MOSI, Q1.G
  N4: Part1.GND, Q1.S, S1.leg0, S2.leg0
  N5: Part1.D5_PWM, Q2.S
  N6: Part1.D6_PWM, Q2.D
  N7: Part1.D7, Q2.G
  N8: Part1.VIN, R1.Pin_0
  N9: Q1.D, R1.Pin_1
